# Fritzing sketch projeto (saved by Fritzing 0.9.3b)
breadboards: 1

parts:
  Componente1 = Arduino Uno (Rev3)
  DHT2 = DHT11 Humitidy and Temperature Sensor
  J1 = double row male pin header, 4 pins [form="♂ (male)"]
  R1 = Resistor [tolerance=±5% resistance=10k package=THT]
  R2 = Resistor [tolerance=±5% resistance=10k package=THT]
  J2 = Piezo Speaker
  LED1 = LED - 5mm [color="Blue (525nm)" package="5 mm [THT]"]
  R4 = Resistor [tolerance=±5% resistance=330 package=THT]
  R5 = Resistor [tolerance=±5% resistance=330 package=THT]
  LED2 = LED - 5mm [color="Green (555nm)" package="5 mm [THT]"]
  R6 = Resistor [tolerance=±5% resistance=10k package=THT]
  LED3 = LED - 5mm [color="Red (633nm)" package="5 mm [THT]"]
  C1 = Ceramic Capacitor [capacitance=100nF package="100 mil [THT, multilayer]"]

nets:
  N1: Componente1.A0, J1.pin4, R1.Pin_0
  GND: Componente1.GND, DHT2.GND, J1.pin2, R1.Pin_1, J2.pin1, R4.Pin_1, R5.Pin_1, R6.Pin_1, C1.0
  N2: Componente1.D2, DHT2.DATA, R2.Pin_1
  N3: Componente1.D3_PWM, LED2.anode
  N4: Componente1.D4, J2.pin2
  N5: Componente1.D5_PWM, LED3.anode
  5V: Componente1.5V, DHT2.VDD, J1.pin1, R2.Pin_0, LED1.anode, C1.1
  N6: LED1.cathode, R6.Pin_0
  N7: R4.Pin_0, LED3.cathode
  N8: R5.Pin_0, LED2.cathode

notes:
  O capacitor cerâmico
  de 100nf . É opcional.
  Este capacitor de desacoplamento filtra
  ruidos indesejáveis na linha de alimentação.
  C1
  100nf
  R1
  10k
  R1 é um resistor de pull down. Este resistor evita que a porta analógica do arduino gere leituras aleatórias, se caso por algum motivo não houver sinal vindo do sensor MQ2 . Isto também previne um possível acionamento fantasma do alarme.
  R2
  10k
  R2 é um resistor de pull up recomendado pelo datasheet do sensor DHT11, quando as conexões são menores que 20m.

custom parts:
  DHT11 Humitidy and Temperature Sensor: DHT11 Humidity and Temperature Sensor
